// Logisim project data_path.circ as structural Verilog: 1 circuit, main circuit main
module main (
  input  [31:0] in_1,
  input  [31:0] in_2,
  input  [31:0] in_3,
  input  [31:0] in_4,
  input  [31:0] in_5,
  input  [31:0] in_6,
  input  [31:0] in_7,
  input  [31:0] in_8,
  input  [31:0] in_9,
  input  [31:0] in_10,
  input  [31:0] in_11,
  input  [31:0] in_12,
  input  [31:0] in_13,
  input  [31:0] in_14,
  input  [31:0] in_15,
  input  [31:0] in_16,
  input  [31:0] in_17,
  input  [31:0] in_18,
  input  [31:0] in_19,
  input  [31:0] in_20,
  input  [31:0] in_21,
  input  [31:0] in_22,
  input  [31:0] in_23,
  input  [31:0] in_24,
  input  [31:0] in_25,
  input  [31:0] in_26,
  input  [31:0] in_27,
  input  [31:0] in_28,
  input  [31:0] in_29,
  input  [31:0] in_30,
  input  [31:0] in_31,
  input  [31:0] in_32,
  input  [31:0] in_33,
  output out_34
);

  wire clock, Extop, jalr, less_flag_signed, less_flag_unsigned, mem_to_reg, Memory_Write, Output_Enable,
       pc_src, read_register_1, RegWrite;
  wire [1:0] ALUsrc;
  wire [4:0] Imm16, ImmL, multiplexer_1_out, RS1;
  wire [7:0] ALU_Op;
  wire [10:0] Funct;
  wire [15:0] Imm_16, instruction;
  wire [19:0] Pc, pc_inc, pc_next;
  wire [31:0] ALU_Result, ALU_result_t, bit_extender_1_out, bit_extender_2_out, bit_extender_3_out,
       bit_extender_4_out, bit_extender_5_out, BusA, BusB, BusW, main_2_memory_output, multiplexer_5_out,
       multiplexer_6_out, RA, Write_Data;

  instruction_mem_main main_1 (.in_1(Pc), .out_2({Funct, Imm16, instruction[15:11], ImmL, instruction[5:0]}));
  data_mem_main main_2 (
    .in_1(ALU_Result), .in_2(Memory_Write), .in_3(Output_Enable), .in_4(clock),
    .memory_output(main_2_memory_output));
  Multiplexer #(.width(5), .enable("false")) multiplexer_1 (
    .in0(RS1), .in1(ImmL), .out(multiplexer_1_out), .sel(read_register_1));
  Clock clock_1 (.out(clock));
  assign bit_extender_1_out = {{12{1'b0}}, pc_inc};  // Bit_Extender bit_extender_1
  Multiplexer #(.width(32), .enable("false")) multiplexer_2 (
    .in0(main_2_memory_output), .in1(ALU_result_t), .out(BusW), .sel(mem_to_reg));
  assign bit_extender_2_out = {{12{1'b0}}, pc_inc};  // Bit_Extender bit_extender_2
  Multiplexer #(.width(32), .enable("false")) multiplexer_3 (
    .in0(BusW), .in1(bit_extender_1_out), .out(Write_Data), .sel(jalr));
  Multiplexer #(.width(32), .enable("false")) multiplexer_4 (
    .in0(BusW), .in1(bit_extender_2_out), .out(Write_Data), .sel(jalr));
  assign bit_extender_3_out = {{16{1'b0}}, {Funct, Imm16}};  // Bit_Extender bit_extender_3
  assign bit_extender_4_out = {{16{Funct[10]}}, {Funct, Imm16}};  // Bit_Extender bit_extender_4
  assign bit_extender_5_out = {{16{Funct[10]}}, {Funct, ImmL}};  // Bit_Extender bit_extender_5
  Multiplexer #(.width(32), .enable("false")) multiplexer_5 (
    .in0(bit_extender_3_out), .in1(bit_extender_4_out), .out(multiplexer_5_out), .sel(Extop));
  // Reg_file reg_file_1: pin names not known; wires that end beside it: multiplexer_1_out, Imm16, ImmL, clock, in_1, in_2, in_4, in_6, in_9, RegWrite, in_11, in_13, in_15, in_17, in_19, in_21, in_23, Write_Data, in_25, in_27, in_29, in_31, in_33, in_3, in_5, in_7, in_10, in_12, in_14, in_16, in_18, in_20, in_22, in_24, in_26, in_28, in_30, in_32, BusA, BusB
  Multiplexer #(.select(2), .width(32), .enable("false")) multiplexer_6 (
    .in0(BusB), .in1(multiplexer_5_out), .in2(bit_extender_5_out), .out(multiplexer_6_out), .sel(ALUsrc));  // open: in3
  pc_circut_main main_3 (
    .pc_src(pc_src), .next_pc(pc_next), .out_9(pc_inc), .Lower5(ImmL), .upper11(Funct), .IMM16(Imm_16),
    .in_3(clock), .RS1(RA), .jalr(jalr));
  ALU_Full J (
    .OverFlow(out_34), .AInvert(ALU_Op[7]), .CarryIn(ALU_Op[6]), .in_2(BusA), .in_4(multiplexer_6_out),
    .Operation(ALU_Op[5:4]), .BInvert(ALU_Op[6]), .select_Alu(ALU_Op[3:0]),
    .less_flag_signed(less_flag_unsigned), .out_11(less_flag_signed), .out_9(ALU_Result));  // open: in_5, out_14, zreo_flag

  assign in_8 = in_7;

  // Other names for the same wires on the sheet: instruction (some bits) = {Funct, Imm16, ImmL}; Rd[4:0] = ImmL;
  //   Imm16[15:5] = Funct; ImmU[10:0] = Funct; OP[5:0] = instruction[5:0]; Rs1_t[4:0] = instruction[15:11];
  //   Rs2[4:0] = Imm16; R0[31:0] = in_1; R1[31:0] = in_2; R2[31:0] = in_4; R3[31:0] = in_6; R4[31:0] = in_9;
  //   R5[31:0] = in_11; R6[31:0] = in_13; R7[31:0] = in_15; R8[31:0] = in_17; R9[31:0] = in_19; R10[31:0] = in_21;
  //   R11[31:0] = in_23; R12[31:0] = in_25; R13[31:0] = in_27; R14[31:0] = in_29; R15[31:0] = in_31;
  //   R16[31:0] = in_33; R17[31:0] = in_3; R18[31:0] = in_5; R19[31:0] = in_7; R20[31:0] = in_10; R21[31:0] = in_12;
  //   R22[31:0] = in_14; R23[31:0] = in_16; R24[31:0] = in_18; R25[31:0] = in_20; R26[31:0] = in_22;
  //   R27[31:0] = in_24; R28[31:0] = in_26; R29[31:0] = in_28; R30[31:0] = in_30; R31[31:0] = in_32

  // Notes on the sheet:
  //   Registers
  //   Instruction_Memory
  //   Data_Memory
  //   Decoding_Instruction
  //   ALU
endmodule
